# Fritzing sketch Sketch (saved by Fritzing 0.9.6b)

parts:
  Part1 = Arduino Uno (Rev3) - ICSP
  DHT1 = DHT22 Humidity and Temperature Sensor
  Part2 = Adafruit BH1750 [part_number="Adafruit #4681"]
  Part3 = INMP441
  Q1 = npn-Powertransistor [package="TO220 [THT]"]
  Q2 = npn-Powertransistor [package="TO220 [THT]"]
  R1 = Resistor [tolerance=±5% resistance=10k package="1206 [SMD]"]
  R2 = Resistor [tolerance=±5% resistance=10k package="1206 [SMD]"]
  Q3 = npn-Powertransistor [package="TO220 [THT]"]
  Q4 = npn-Powertransistor [package="TO220 [THT]"]
  Q5 = npn-Powertransistor [package="TO220 [THT]"]
  R3 = Resistor [tolerance=±5% resistance=10k package="1206 [SMD]"]
  R4 = Resistor [tolerance=±5% resistance=10k package="1206 [SMD]"]
  R6 = Resistor [tolerance=±5% resistance=10k package="1206 [SMD]"]
  U1 = Luxeon LED [package=luxeon]
  U2 = Luxeon LED [package=luxeon]
  U3 = Luxeon LED [package=luxeon]
  U4 = Luxeon LED [package=luxeon]
  VCC1 = Battery block 9V

nets:
  N1: Part1.A4/SDA, Part2.SDA, Part2.ADDR, Part3.SD
  N2: Part1.A5/SCL, Part2.SCL, Part3.SCK
  VDD: Part1.5V, DHT1.VDD, Part2.VCC, Part2.3.3V, Part3.VDD
  N3: Part1.ICSP_MOSI, Part1.D11_PWM/MOSI, R1.Pin_1
  GND: Part1.GND, DHT1.GND, Part2.GND, Part3.GND, Q1.emitter, Q2.emitter, Q3.emitter, Q4.emitter, Q5.emitter, VCC1.-
  N4: Part1.D9_PWM, R3.Pin_1
  N5: Part1.D10_PWM/SS, R2.Pin_1
  N6: Part1.D2, DHT1.DATA
  N7: Part1.D5_PWM, R6.Pin_1
  N8: Part1.D6_PWM, R4.Pin_1
  N9: Q1.base, R1.Pin_0
  N10: Q1.collector, U1.C
  N11: Q2.base, R2.Pin_0
  N12: Q2.collector, U2.C
  N13: Q3.base, R3.Pin_0
  N14: Q3.collector, U3.C
  N15: Q4.base, R4.Pin_0
  N16: Q4.collector, U4.C
  N17: Q5.base, R6.Pin_0
  N18: U1.A, U2.A, U3.A, U4.A, VCC1.+

custom parts:
  Adafruit BH1750: This is the BH1750 16-bit Ambient Light sensor from Rohm. Because of how important it is to humans and most other living things, sensing the amount of light in an environment is a common place to get started when learning to work with microcontrollers and sensors. Should we turn up the brightness of our display or dim it to save power? Which direction should your robot move to stay in an area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
  INMP441: This is a simple breakout board for the INMP441 I2S MEMS microphone.
